// Logisim project AND_GATE.circ as structural Verilog: 1 circuit, main circuit main
module main (
  input  X,
  input  Y
);

  wire and_1_out;

  and and_1 (and_1_out, X, Y);
  LED led_1 (.in(and_1_out));
endmodule
