// Logisim project Ff.circ as structural Verilog: 1 circuit, main circuit main
module main (
  input  [15:0] A,
  input  [15:0] B,
  input  [4:0] in_3,
  input  [4:0] in_4,
  input  [5:0] in_5
);

  wire comparator_1_gt, comparator_2_eq, comparator_3_gt, comparator_4_eq, not_2_out, not_3_out, not_5_out,
       not_6_out, SB, SS;
  wire [4:0] EB, ES, subtractor_1_out;
  wire [10:0] adder_1_out, MB, MS, MSS, multiplexer_1_out, multiplexer_4_out, subtractor_2_out;
  wire [10:10] M1, M2;
  wire [11:0] multiplexer_8_out;
  wire [11:11] adder_1_cout, subtractor_2_bout;
  wire [16:11] shifter_1_out;

  Comparator #(.mode("unsigned"), .width(11)) comparator_1 (.a(MB), .b(MSS), .gt(comparator_1_gt));  // open: eq, lt
  not not_1 (M1[10], comparator_2_eq);
  Comparator #(.mode("unsigned"), .width(5)) comparator_2 (.a(A[5:1]), .b(in_3), .eq(comparator_2_eq));  // open: gt, lt
  Comparator #(.mode("unsigned"), .width(5)) comparator_3 (
    .a(A[5:1]), .b(B[5:1]), .gt(comparator_3_gt));  // open: eq, lt
  Multiplexer #(.width(11)) multiplexer_1 (.in0(MSS), .in1(MB), .out(multiplexer_1_out), .sel(comparator_1_gt));
  not not_2 (not_2_out, comparator_3_gt);
  Multiplexer #(.width(5)) multiplexer_2 (.in0(B[5:1]), .in1(A[5:1]), .out(EB), .sel(comparator_3_gt));
  Multiplexer #(.width(5)) multiplexer_3 (.in0(B[5:1]), .in1(A[5:1]), .out(ES), .sel(not_2_out));
  not not_3 (not_3_out, comparator_1_gt);
  Multiplexer #(.width(11)) multiplexer_4 (.in0(MSS), .in1(MB), .out(multiplexer_4_out), .sel(not_3_out));
  Subtractor #(.width(5)) subtractor_1 (.a(EB), .b(ES), .out(subtractor_1_out));  // open: bin, bout
  Adder #(.width(11)) adder_1 (
    .a(multiplexer_1_out), .b(multiplexer_4_out), .out(adder_1_out), .cout(adder_1_cout[11]));  // open: cin
  Subtractor #(.width(11)) subtractor_2 (
    .a(multiplexer_1_out), .b(multiplexer_4_out), .out(subtractor_2_out), .bout(subtractor_2_bout[11]));  // open: bin
  not not_4 (M2[10], comparator_4_eq);
  Comparator #(.mode("unsigned"), .width(5)) comparator_4 (.a(B[5:1]), .b(in_4), .eq(comparator_4_eq));  // open: gt, lt
  not not_5 (not_5_out, comparator_3_gt);
  Multiplexer #(.width(11)) multiplexer_5 (
    .in0({M2[10], B[15:6]}), .in1({M1[10], A[15:6]}), .out(MB), .sel(comparator_3_gt));
  Multiplexer #(.width(11)) multiplexer_6 (.in0({M2[10], B[15:6]}), .in1({M1[10], A[15:6]}), .out(MS), .sel(not_5_out));
  Multiplexer multiplexer_7 (.in0(B[0]), .in1(A[0]), .out(SB), .sel(comparator_3_gt));
  Multiplexer #(.select(2), .width(12)) multiplexer_8 (
    .in0({adder_1_cout[11], adder_1_out}), .in1({subtractor_2_bout[11], subtractor_2_out}),
    .in2({subtractor_2_bout[11], subtractor_2_out}), .in3({adder_1_cout[11], adder_1_out}),
    .out(multiplexer_8_out), .sel({A[0], B[0]}));
  not not_6 (not_6_out, comparator_3_gt);
  Multiplexer multiplexer_9 (.in0(B[0]), .in1(A[0]), .out(SS), .sel(not_6_out));
  Shifter #(.shift("lr"), .width(17)) shifter_1 (
    .in({in_5, MS}), .\dist (subtractor_1_out), .out({shifter_1_out, MSS}));

  // Other names for the same wires on the sheet: S1 = A[0]; E1[4:0] = A[5:1]; S2 = B[0]; E2[4:0] = B[5:1];
  //   M1[9:0] = A[15:6]; M2[9:0] = B[15:6]
endmodule
