// Logisim project Processor_mufed.circ as structural Verilog: 5 circuits, main circuit main
module main (
  input  [7:0] in_1
);

  wire alu_1_zero, and_1_out, CLK, controlunit_1_alusrc, controlunit_1_branch, controlunit_1_branchtype,
       controlunit_1_jump, controlunit_1_memread, controlunit_1_memtoreg, controlunit_1_memwrite,
       controlunit_1_regdst, controlunit_1_regwrite, xor_1_out;
  wire [2:0] controlunit_1_aluop;
  wire [3:0] alu_1_result, DataMemory_dout, multiplexer_1_out, multiplexer_2_out, multiplexer_5_out,
       registerfile_1_readdata1, registerfile_1_readdata2;
  wire [7:0] adder_1_out, adder_2_out, adder_3_out, bit_extender_1_out, ext, JMP, multiplexer_3_out,
       multiplexer_4_out, PC_q;
  wire [15:0] InstrMem_data;

  Clock clock_1 (.out(CLK));
  Register PC (.D(multiplexer_4_out), .en(1'b1), .clk(CLK), .Q(PC_q));  // open: clr
  Adder adder_1 (.a(PC_q), .b(8'h1), .out(adder_1_out), .cin(1'b0));  // open: cout
  ROM #(.dataWidth(16)) InstrMem (.addr(PC_q), .data({InstrMem_data[15:12], JMP, InstrMem_data[3:0]}));
  Multiplexer #(.width(4)) multiplexer_1 (
    .in0(JMP[3:0]), .in1(InstrMem_data[3:0]), .out(multiplexer_1_out), .sel(controlunit_1_regdst));
  ControlUnit controlunit_1 (
    .OP(InstrMem_data[15:12]), .RegWrite(controlunit_1_regwrite), .RegDst(controlunit_1_regdst),
    .ALUSrc(controlunit_1_alusrc), .ALUOp(controlunit_1_aluop), .MemRead(controlunit_1_memread),
    .MemWrite(controlunit_1_memwrite), .MemToReg(controlunit_1_memtoreg), .Branch(controlunit_1_branch),
    .BranchType(controlunit_1_branchtype), .Jump(controlunit_1_jump));
  Adder adder_2 (.a(adder_1_out), .b(ext), .out(adder_2_out), .cin(1'b0));  // open: cout
  RegisterFile registerfile_1 (
    .RegWrite(controlunit_1_regwrite), .ReadReg1(JMP[7:4]), .ReadReg2(JMP[3:0]),
    .WriteReg(multiplexer_1_out), .WriteData(multiplexer_5_out), .CLK(CLK),
    .ReadData1(registerfile_1_readdata1), .ReadData2(registerfile_1_readdata2));
  Multiplexer #(.width(4)) multiplexer_2 (
    .in0(registerfile_1_readdata2), .in1(InstrMem_data[3:0]), .out(multiplexer_2_out),
    .sel(controlunit_1_alusrc));
  xor xor_1 (xor_1_out, controlunit_1_branchtype, alu_1_zero);
  assign bit_extender_1_out = {{4{1'b0}}, registerfile_1_readdata1};  // Bit_Extender bit_extender_1
  assign ext = {{4{InstrMem_data[3]}}, InstrMem_data[3:0]};  // Bit_Extender bit_extender_2
  and and_1 (and_1_out, controlunit_1_branch, xor_1_out);
  Adder adder_3 (.a(bit_extender_1_out), .b(ext), .out(adder_3_out), .cin(1'b0));  // open: cout
  Multiplexer #(.width(8)) multiplexer_3 (
    .in0(adder_1_out), .in1(adder_2_out), .out(multiplexer_3_out), .sel(and_1_out));
  ALU alu_1 (
    .A(registerfile_1_readdata1), .B(multiplexer_2_out), .ALUOp(controlunit_1_aluop), .Zero(alu_1_zero),
    .Result(alu_1_result));
  Multiplexer #(.width(8)) multiplexer_4 (
    .in0(multiplexer_3_out), .in1(JMP), .out(multiplexer_4_out), .sel(controlunit_1_jump));
  RAM #(.asyncread("true"), .dataWidth(4)) DataMemory (
    .addr(adder_3_out), .we(controlunit_1_memwrite), .oe(controlunit_1_memread), .clk(CLK),
    .din(registerfile_1_readdata2), .dout(DataMemory_dout));
  Multiplexer #(.width(4)) multiplexer_5 (
    .in0(alu_1_result), .in1(DataMemory_dout), .out(multiplexer_5_out), .sel(controlunit_1_memtoreg));

  // Notes on the sheet:
  //   contents of InstrMem (hex, n*v repeats v):
  //   2015 2023 6123 d124 1152 f123 3131 7123 e132 8123 131 9131 4010 c040 a111 205f 2051 b121 205e 5150
  //   205d 6120 2057
endmodule

module RegisterFile (
  input  RegWrite,
  input  [3:0] ReadReg1,
  input  [3:0] ReadReg2,
  input  [3:0] WriteReg,
  input  [3:0] WriteData,
  input  CLK,
  output [3:0] ReadData1,
  output [3:0] ReadData2
);

  wire and_1_out, not_1_out, not_2_out, not_3_out;
  wire [3:0] regarray_1_q0, regarray_1_q1, regarray_1_q2, regarray_1_q3, regarray_1_q4;
  wire [4:0] decoder_1_out1;

  and and_1 (and_1_out, RegWrite, not_1_out);
  not not_1 (not_1_out, WriteReg[3]);
  not not_2 (not_2_out, ReadReg1[3]);
  not not_3 (not_3_out, ReadReg2[3]);
  Decoder #(.select(3)) decoder_1 (
    .out1(decoder_1_out1[0]), .out2(decoder_1_out1[1]), .out3(decoder_1_out1[2]), .out4(decoder_1_out1[3]),
    .out5(decoder_1_out1[4]), .sel(WriteReg[2:0]), .en(and_1_out));  // open: out0, out6, out7
  Multiplexer #(.enable("true"), .select(3), .width(4)) multiplexer_1 (
    .in0(4'b0000), .in1(regarray_1_q0), .in2(regarray_1_q1), .in3(regarray_1_q2), .in4(regarray_1_q3),
    .in5(regarray_1_q4), .in6(4'b0000), .in7(4'b0000), .out(ReadData1), .sel(ReadReg1[2:0]), .en(not_2_out));
  Multiplexer #(.enable("true"), .select(3), .width(4)) multiplexer_2 (
    .in0(4'b0000), .in1(regarray_1_q0), .in2(regarray_1_q1), .in3(regarray_1_q2), .in4(regarray_1_q3),
    .in5(regarray_1_q4), .in6(4'b0000), .in7(4'b0000), .out(ReadData2), .sel(ReadReg2[2:0]), .en(not_3_out));
  RegArray regarray_1 (
    .D(WriteData), .WE(decoder_1_out1), .CLK(CLK), .q0(regarray_1_q0), .q1(regarray_1_q1),
    .q2(regarray_1_q2), .q3(regarray_1_q3), .q4(regarray_1_q4));
endmodule

module RegArray (
  input  [3:0] D,
  input  [4:0] WE,
  input  CLK,
  output [3:0] q0,
  output [3:0] q1,
  output [3:0] q2,
  output [3:0] q3,
  output [3:0] q4
);

  Register #(.width(4)) t0 (.D(D), .en(WE[0]), .clk(CLK), .Q(q0));  // open: clr
  Register #(.width(4)) t1 (.D(D), .en(WE[1]), .clk(CLK), .Q(q1));  // open: clr
  Register #(.width(4)) t2 (.D(D), .en(WE[2]), .clk(CLK), .Q(q2));  // open: clr
  Register #(.width(4)) t3 (.D(D), .en(WE[3]), .clk(CLK), .Q(q3));  // open: clr
  Register #(.width(4)) t4 (.D(D), .en(WE[4]), .clk(CLK), .Q(q4));  // open: clr
endmodule

module ControlUnit (
  input  [3:0] OP,
  output RegWrite,
  output RegDst,
  output ALUSrc,
  output [2:0] ALUOp,
  output MemRead,
  output MemWrite,
  output MemToReg,
  output Branch,
  output BranchType,
  output Jump
);

  wire [15:12] rom_1_data;

  ROM #(.addrWidth(4), .dataWidth(16)) rom_1 (
    .addr(OP),
    .data({rom_1_data, RegWrite, RegDst, ALUSrc, ALUOp, MemRead, MemWrite, MemToReg, Branch, BranchType, Jump}));

  // Notes on the sheet:
  //   contents of rom_1 (hex, n*v repeats v):
  //   b40 a40 a00 a80 210 1 c00 cc0 d00 b80 44 46 a28 c40 ac0 c80
endmodule

module ALU (
  input  [3:0] A,
  input  [3:0] B,
  input  [2:0] ALUOp,
  output Zero,
  output [3:0] Result
);

  wire or_2_out;
  wire [3:0] adder_1_out, and_1_out, nor_1_out, or_1_out, shifter_1_out, shifter_2_out, xor_1_out;

  xor xor_1 (xor_1_out[0], B[0], ALUOp[0]);
  xor xor_2 (xor_1_out[1], B[1], ALUOp[0]);
  xor xor_3 (xor_1_out[2], B[2], ALUOp[0]);
  xor xor_4 (xor_1_out[3], B[3], ALUOp[0]);
  Adder #(.width(4)) adder_1 (.a(A), .b(xor_1_out), .out(adder_1_out), .cin(ALUOp[0]));  // open: cout
  assign and_1_out = A & B;  // AND_Gate and_1, 4 bits wide
  assign or_1_out = A | B;  // OR_Gate or_1, 4 bits wide
  assign nor_1_out = ~(A | B);  // NOR_Gate nor_1, 4 bits wide
  Shifter #(.width(4)) shifter_1 (.in(A), .\dist (B[1:0]), .out(shifter_1_out));
  Shifter #(.shift("lr"), .width(4)) shifter_2 (.in(A), .\dist (B[1:0]), .out(shifter_2_out));
  Multiplexer #(.select(3), .width(4)) multiplexer_1 (
    .in0(adder_1_out), .in1(adder_1_out), .in2(and_1_out), .in3(or_1_out), .in4(nor_1_out),
    .in5(shifter_1_out), .in6(shifter_2_out), .in7(4'b0000), .out(Result), .sel(ALUOp));
  or or_2 (or_2_out, adder_1_out[0], adder_1_out[1], adder_1_out[2], adder_1_out[3]);
  not not_1 (Zero, or_2_out);
endmodule
